# Fritzing sketch stone_lcd (saved by Fritzing 0.9.3b)
breadboards: 1

parts:
  Q1 = NPN-Transistor [package="TO92 [THT]"]
  Q2 = NPN-Transistor [package="TO92 [THT]"]
  R1 = Resistor [tolerance=±5% resistance=4.7k package="0603 [SMD]"]
  R2 = Resistor [tolerance=±5% resistance=10k package="0603 [SMD]"]
  JP1 = Header 4 [package=screwterminal-3.5mm-4_lock]
  Part1 = Arduino Nano (Rev3.0)
  R3 = Resistor [tolerance=±5% resistance=4.7k package="0603 [SMD]"]
  R4 = Resistor [tolerance=±5% resistance=10k package="0603 [SMD]"]
  J1 = Power Jack [package=power_jack_pth_lock]
  LED1 = smd LED [color="Red (633nm)" package="1206 [SMD]"]
  LED2 = smd LED [color="Red (633nm)" package="1206 [SMD]"]
  LED3 = smd LED [color="Red (633nm)" package="1206 [SMD]"]
  R5 = Resistor [tolerance=±5% resistance=220 package="0603 [SMD]"]
  R6 = Resistor [tolerance=±5% resistance=220 package="0603 [SMD]"]
  R7 = Resistor [tolerance=±5% resistance=220 package="0603 [SMD]"]
  U1 = POT [package=pot_mammoth]

nets:
  GND: Q1.E, Q2.E, JP1.4, Part1.GND, J1.GND, R5.Pin_1, R6.Pin_1, R7.Pin_1, U1.S
  N1: Q1.B, R3.Pin_0
  N2: Q1.C, R2.Pin_1, Part1.D2
  N3: Q2.B, R1.Pin_0
  N4: Q2.C, JP1.2, R4.Pin_1
  N5: R1.Pin_1, Part1.D3
  N6: R2.Pin_0, Part1.5V, U1.E
  N7: JP1.1, J1.PWR
  N8: JP1.3, R3.Pin_1
  N9: Part1.D11/MOSI, LED3.anode
  N10: Part1.D12/MISO, LED2.anode
  N11: Part1.A0, U1.A
  N12: Part1.D13/SCK, LED1.anode
  N13: LED1.cathode, R5.Pin_0
  N14: LED2.cathode, R6.Pin_0
  N15: LED3.cathode, R7.Pin_0

notes:
  STONE LCD
  +12V/RX/TX/GND
  DC POWER
  GND/+12V
  Transistor BC547
  Fritzing Pin: E-B-C
