# Fritzing sketch stone_lcd_pico (saved by Fritzing 0.9.3b)
breadboards: 1

parts:
  Q1 = NPN-Transistor [package="TO92 [THT]"]
  Q2 = NPN-Transistor [package="TO92 [THT]"]
  R1 = Resistor [tolerance=±5% resistance=4.7k package="0603 [SMD]"]
  R2 = Resistor [tolerance=±5% resistance=10k package="0603 [SMD]"]
  JP1 = Header 4 [package=screwterminal-3.5mm-4_lock]
  R3 = Resistor [tolerance=±5% resistance=4.7k package="0603 [SMD]"]
  R4 = Resistor [tolerance=±5% resistance=10k package="0603 [SMD]"]
  J1 = Power Jack [package=power_jack_pth_lock]
  LED1 = smd LED [color="Red (633nm)" package="1206 [SMD]"]
  LED2 = smd LED [color="Red (633nm)" package="1206 [SMD]"]
  LED3 = smd LED [color="Red (633nm)" package="1206 [SMD]"]
  R5 = Resistor [tolerance=±5% resistance=220 package="0603 [SMD]"]
  R6 = Resistor [tolerance=±5% resistance=220 package="0603 [SMD]"]
  R7 = Resistor [tolerance=±5% resistance=220 package="0603 [SMD]"]
  U1 = POT [package=pot_mammoth]
  Mod1 = Raspberry Pi Pico

nets:
  N1: Q1.E, Q2.E, JP1.4, J1.GND, R6.Pin_1, R7.Pin_1, U1.S, Mod1.pin_3, Mod1.pin_8, Mod1.pin_13, Mod1.pin_18, Mod1.pin_23, Mod1.pin_28, Mod1.pin_33, Mod1.pin_38
  N2: Q1.B, R3.Pin_0
  N3: Q1.C, R2.Pin_1, Mod1.pin_11
  N4: Q2.B, R1.Pin_0
  N5: Q2.C, JP1.2, R4.Pin_1
  N6: R1.Pin_1, Mod1.pin_10
  N7: R2.Pin_0, U1.E, Mod1.pin_36
  N8: JP1.1, J1.PWR
  N9: JP1.3, R3.Pin_1
  N10: LED1.cathode, R5.Pin_0
  N11: LED1.anode, Mod1.pin_24
  N12: LED2.cathode, R6.Pin_0
  N13: LED2.anode, Mod1.pin_26
  N14: LED3.cathode, R7.Pin_0
  N15: LED3.anode, Mod1.pin_25
  N16: U1.A, Mod1.pin_34

notes:
  STONE LCD
  +12V/RX/TX/GND
  DC POWER
  GND/+12V
  Transistor BC547
  Fritzing Pin: E-B-C

custom parts:
  Raspberry Pi Pico: Raspberry Pi Pico. Based around the RP2040 microcontroller the Pico is a low cost microcontroller device bringing Raspberry Pi quality, cost, and easy of use to the microcontroller space. Jan 2021, Split part in to two versions: tht (this one) and SMD. This one will drill holes for a .1 in header in pcb to allow plugging in the module as well as providing pads to solder the module to the top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
