# Fritzing sketch circuit (saved by Fritzing 0.9.3b)
breadboards: 1

parts:
  M1 = STM32F103C8T6 blue mini board
  R1 = Resistor [tolerance=±5% resistance=220 package=THT]
  LED1 = smd LED [color="Red (633nm)" package="0603 [SMD]"]
  R2 = Resistor [tolerance=±5% resistance=220 package=THT]
  LED2 = smd LED [color="Red (633nm)" package="0603 [SMD]"]
  R3 = Resistor [tolerance=±5% resistance=220 package=THT]
  LED3 = smd LED [color="Red (633nm)" package="0603 [SMD]"]
  R4 = Resistor [tolerance=±5% resistance=220 package=THT]
  LED4 = smd LED [color="Red (633nm)" package="0603 [SMD]"]
  U1 = RS232 Transceiver [package=dil16]
  C1 = Electrolytic Capacitor [capacitance=10μF package="0605 [SMD, electrolytic]"]
  C2 = Electrolytic Capacitor [capacitance=10μF package="0605 [SMD, electrolytic]"]
  C3 = Electrolytic Capacitor [capacitance=10μF package="0605 [SMD, electrolytic]"]  # not connected
  JP1 = Header 4 [package=molex-1x4_lock]
  C4 = Electrolytic Capacitor [capacitance=10μF package="0605 [SMD, electrolytic]"]
  R5 = Rotary Potentiometer (Large) [maximum_resistance=100kΩ package=THT]
  J1 = Power Jack [package=power_jack_combo]

nets:
  N1: M1.B12, R4.Pin_1
  N2: M1.B13, R3.Pin_1
  N3: M1.B14, R2.Pin_1
  GND: M1.G, M1.GND, U1.GND, JP1.4, R5.leg2, J1.GND
  N4: M1.3.3V, R5.leg1
  N5: M1.A0, R5.wiper
  N6: M1.A1, U1.T2IN
  N7: M1.A2, U1.R2OUT
  N8: M1.A6, R1.Pin_1
  N9: R1.Pin_0, LED1.anode
  N10: R2.Pin_0, LED2.anode
  N11: R3.Pin_0, LED3.anode
  N12: R4.Pin_0, LED4.anode
  N13: U1.C1+, C1.+
  N14: U1.V+, C4.+
  N15: U1.C1-, C1.-
  N16: U1.C2+, C2.+
  N17: U1.C2-, C2.-
  N18: U1.T2OUT, JP1.3
  N19: U1.R2IN, JP1.2
  N20: U1.VCC, C4.-
  N21: JP1.1, J1.GNDBREAK

notes:
  +12V | RX | TX | GND
  GND
  +5V
  GND
  +3.3V
